// Logisim project comparator ic.circ as structural Verilog: 2 circuits, main circuit main
module main (
  input  A,
  input  B,
  output A___B,
  output A___B_2,
  output A___B_3
);

  wire not_1_out, not_2_out;

  not not_1 (not_1_out, B);
  not not_2 (not_2_out, A);
  and and_1 (A___B, A, not_1_out);
  xnor xnor_1 (A___B_2, A, B);
  and and_2 (A___B_3, B, not_2_out);
endmodule

module comaparator_ic (
);

  main main_1 ();  // open: A, B, A___B, A___B_2, A___B_3
  main main_2 ();  // open: A, B, A___B, A___B_2, A___B_3
endmodule
