// Logisim project flip flop ic.circ as structural Verilog: 2 circuits, main circuit main
module main (
  input  in_1,
  input  in_2,
  output out_3,
  output out_4
);

  wire nand_1_out, nand_2_out;

  nand nand_1 (nand_1_out, in_1, in_2);
  nand nand_2 (nand_2_out, nand_1_out, in_2);
  nand nand_3 (out_3, nand_1_out, out_4);
  nand nand_4 (out_4, out_3, nand_2_out);
endmodule

module flip_flop_ic (
  input  in_1,
  input  in_2,
  output out_3
);

  wire main_1_out_3, main_2_out_3, main_3_out_3;

  main main_1 (.in_1(in_1), .in_2(in_2), .out_3(main_1_out_3));  // open: out_4
  main main_2 (.in_1(main_1_out_3), .in_2(in_2), .out_3(main_2_out_3));  // open: out_4
  main main_3 (.in_1(main_2_out_3), .in_2(in_2), .out_3(main_3_out_3));  // open: out_4
  main main_4 (.in_1(main_3_out_3), .in_2(in_2), .out_3(out_3));  // open: out_4
endmodule
