// Logisim project half and full adder.circ as structural Verilog: 1 circuit, main circuit main
module main (
  input  A,
  input  B,
  input  A_2,
  input  B_2,
  input  C_in,
  output carry,
  output sum,
  output Sum_2,
  output out_9
);

  wire and_2_out, and_3_out, xor_2_out;

  and and_1 (carry, A, B);
  xor xor_1 (sum, A, A);
  xor xor_2 (xor_2_out, A_2, B_2);
  and and_2 (and_2_out, C_in, xor_2_out);
  and and_3 (and_3_out, A_2, B_2);
  xor xor_3 (Sum_2, xor_2_out, C_in);
  or or_1 (out_9, and_2_out, and_3_out);

  // Notes on the sheet:
  //   Half Adder
  //   Full Adder
endmodule
