// Logisim project multiplexer.circ as structural Verilog: 1 circuit, main circuit main
module main (
  input  I0,
  input  I1,
  input  A,
  output out_4
);

  wire nand_1_out, nand_2_out, nand_3_out;

  nand nand_1 (nand_1_out, A, A);
  nand nand_2 (nand_2_out, I0, A);
  nand nand_3 (nand_3_out, nand_1_out, I1);
  nand nand_4 (out_4, nand_2_out, nand_3_out);
endmodule
