// Logisim project mux with ic.circ as structural Verilog: 2 circuits, main circuit main
module main (
  input  I0,
  input  I1,
  input  A,
  output out_4
);

  wire nand_1_out, nand_2_out, nand_3_out;

  nand nand_1 (nand_1_out, A, A);
  nand nand_2 (nand_2_out, I0, A);
  nand nand_3 (nand_3_out, nand_1_out, I1);
  nand nand_4 (out_4, nand_2_out, nand_3_out);
endmodule

module mux (
  input  in_1,
  input  in_2,
  input  in_3,
  input  in_4,
  input  in_5,
  input  in_6,
  output out_7
);

  wire main_1_out_4, main_2_out_4;

  main main_1 (.I0(in_1), .I1(in_2), .A(in_5), .out_4(main_1_out_4));
  main main_2 (.I0(in_3), .I1(in_4), .A(in_5), .out_4(main_2_out_4));
  main main_3 (.I0(main_1_out_4), .I1(main_2_out_4), .A(in_6), .out_4(out_7));
endmodule
