// Logisim project fetch unit circuit diagram.circ as structural Verilog: 1 circuit, main circuit main
module main (
  input  in_1,
  input  in_2,
  input  in_3,
  output [31:0] out_4
);

  wire clock_1_out;
  wire [31:0] adder_1_out;

  Clock clock_1 (.out(clock_1_out));
  Register #(.width(32)) register_1 (.D(adder_1_out), .Q(out_4), .clk(clock_1_out), .clr(in_3));  // open: en
  Adder #(.width(32)) adder_1 (.a(out_4), .b(32'h4), .out(adder_1_out));  // open: cin, cout
  ROM #(.addrWidth(24), .dataWidth(32)) rom_1 (.addr(out_4[23:0]), .sel(in_2));  // open: data
endmodule
