// Logisim project regiter-file.circ as structural Verilog: 1 circuit, main circuit main
module main (
  input  [4:0] in_1,
  input  [4:0] in_2
);

  wire [31:0] demultiplexer_1_out0, demultiplexer_1_out1, demultiplexer_1_out2, demultiplexer_1_out3,
       demultiplexer_1_out4, demultiplexer_1_out5, demultiplexer_1_out6, demultiplexer_1_out7,
       demultiplexer_1_out8, demultiplexer_1_out9, demultiplexer_1_out10, demultiplexer_1_out11,
       demultiplexer_1_out12, demultiplexer_1_out13, demultiplexer_1_out14, demultiplexer_1_out15,
       demultiplexer_1_out16, demultiplexer_1_out17, demultiplexer_1_out18, demultiplexer_1_out19,
       demultiplexer_1_out20, demultiplexer_1_out21, demultiplexer_1_out22, demultiplexer_1_out23,
       demultiplexer_1_out24, demultiplexer_1_out25, demultiplexer_1_out26, demultiplexer_1_out27,
       demultiplexer_1_out28, demultiplexer_1_out29, demultiplexer_1_out30, demultiplexer_1_out31,
       demultiplexer_2_out0, demultiplexer_2_out1, demultiplexer_2_out2, or_1_out, or_3_out, or_4_out,
       or_5_out, or_6_out, or_7_out, or_8_out, or_9_out, or_10_out, or_11_out, or_12_out, or_13_out,
       or_14_out, or_15_out, or_16_out, or_17_out, or_18_out, or_19_out, or_20_out, or_21_out, or_22_out,
       or_23_out, or_24_out, or_25_out, or_26_out, or_27_out, or_28_out, or_29_out, or_30_out, or_31_out,
       or_32_out;

  Demultiplexer #(.select(5), .width(32)) demultiplexer_1 (
    .out0(demultiplexer_1_out0), .out1(demultiplexer_1_out1), .out2(demultiplexer_1_out2),
    .out3(demultiplexer_1_out3), .out4(demultiplexer_1_out4), .out5(demultiplexer_1_out5),
    .out6(demultiplexer_1_out6), .out7(demultiplexer_1_out7), .out8(demultiplexer_1_out8),
    .out9(demultiplexer_1_out9), .out10(demultiplexer_1_out10), .out11(demultiplexer_1_out11),
    .out12(demultiplexer_1_out12), .out13(demultiplexer_1_out13), .out14(demultiplexer_1_out14),
    .out15(demultiplexer_1_out15), .out16(demultiplexer_1_out16), .out17(demultiplexer_1_out17),
    .out18(demultiplexer_1_out18), .out19(demultiplexer_1_out19), .out20(demultiplexer_1_out20),
    .out21(demultiplexer_1_out21), .out22(demultiplexer_1_out22), .out23(demultiplexer_1_out23),
    .out24(demultiplexer_1_out24), .out25(demultiplexer_1_out25), .out26(demultiplexer_1_out26),
    .out27(demultiplexer_1_out27), .out28(demultiplexer_1_out28), .out29(demultiplexer_1_out29),
    .out30(demultiplexer_1_out30), .out31(demultiplexer_1_out31), .sel(in_1));  // open: in, en
  Demultiplexer #(.select(5), .width(32)) demultiplexer_2 (
    .out0(demultiplexer_2_out0), .out1(demultiplexer_2_out1), .out2(demultiplexer_2_out2), .sel(in_2));  // open: out3, out4, out5, out6, out7, out8, out9, out10, out11, out12, out13, out14, out15, out16, out17, out18, out19, out20, out21, out22, out23, out24, out25, out26, out27, out28, out29, out30, out31, in, en
  assign or_1_out = demultiplexer_1_out0 | demultiplexer_2_out0;  // OR_Gate or_1, 32 bits wide
  assign demultiplexer_2_out1 = demultiplexer_1_out1 | demultiplexer_2_out1;  // OR_Gate or_2, 32 bits wide
  assign or_3_out = demultiplexer_1_out2 | demultiplexer_2_out2;  // OR_Gate or_3, 32 bits wide
  assign or_4_out = demultiplexer_1_out3;  // OR_Gate or_4, 32 bits wide OR_Gate
  assign or_5_out = demultiplexer_1_out4;  // OR_Gate or_5, 32 bits wide OR_Gate
  assign or_6_out = demultiplexer_1_out5;  // OR_Gate or_6, 32 bits wide OR_Gate
  assign or_7_out = demultiplexer_1_out6;  // OR_Gate or_7, 32 bits wide OR_Gate
  assign or_8_out = demultiplexer_1_out7;  // OR_Gate or_8, 32 bits wide OR_Gate
  assign or_9_out = demultiplexer_1_out8;  // OR_Gate or_9, 32 bits wide OR_Gate
  assign or_10_out = demultiplexer_1_out10;  // OR_Gate or_10, 32 bits wide OR_Gate
  assign or_11_out = demultiplexer_1_out11;  // OR_Gate or_11, 32 bits wide OR_Gate
  assign or_12_out = demultiplexer_1_out12;  // OR_Gate or_12, 32 bits wide OR_Gate
  assign or_13_out = demultiplexer_1_out13;  // OR_Gate or_13, 32 bits wide OR_Gate
  assign or_14_out = demultiplexer_1_out14;  // OR_Gate or_14, 32 bits wide OR_Gate
  assign or_15_out = demultiplexer_1_out15;  // OR_Gate or_15, 32 bits wide OR_Gate
  assign or_16_out = demultiplexer_1_out16;  // OR_Gate or_16, 32 bits wide OR_Gate
  assign or_17_out = demultiplexer_1_out17;  // OR_Gate or_17, 32 bits wide OR_Gate
  assign or_18_out = demultiplexer_1_out18;  // OR_Gate or_18, 32 bits wide OR_Gate
  assign or_19_out = demultiplexer_1_out19;  // OR_Gate or_19, 32 bits wide OR_Gate
  assign or_20_out = demultiplexer_1_out20;  // OR_Gate or_20, 32 bits wide OR_Gate
  assign or_21_out = demultiplexer_1_out21;  // OR_Gate or_21, 32 bits wide OR_Gate
  assign or_22_out = demultiplexer_1_out22;  // OR_Gate or_22, 32 bits wide OR_Gate
  assign or_23_out = demultiplexer_1_out23;  // OR_Gate or_23, 32 bits wide OR_Gate
  assign or_24_out = demultiplexer_1_out24;  // OR_Gate or_24, 32 bits wide OR_Gate
  assign or_25_out = demultiplexer_1_out25;  // OR_Gate or_25, 32 bits wide OR_Gate
  assign or_26_out = demultiplexer_1_out26;  // OR_Gate or_26, 32 bits wide OR_Gate
  assign or_27_out = demultiplexer_1_out27;  // OR_Gate or_27, 32 bits wide OR_Gate
  assign or_28_out = demultiplexer_1_out28;  // OR_Gate or_28, 32 bits wide OR_Gate
  assign or_29_out = demultiplexer_1_out29;  // OR_Gate or_29, 32 bits wide OR_Gate
  assign or_30_out = demultiplexer_1_out30;  // OR_Gate or_30, 32 bits wide OR_Gate
  assign or_31_out = demultiplexer_1_out31;  // OR_Gate or_31, 32 bits wide OR_Gate
  assign or_32_out = demultiplexer_1_out9;  // OR_Gate or_32, 32 bits wide OR_Gate
  Register #(.width(32)) register_1 (.D({32{1'b0}}), .en(or_1_out[0]));  // open: Q, clk, clr
  Register #(.width(32)) register_2 (.en(demultiplexer_2_out1[0]));  // open: D, Q, clk, clr
  Register #(.width(32)) register_3 (.en(or_3_out[0]));  // open: D, Q, clk, clr
  Register #(.width(32)) register_4 (.en(or_4_out[0]));  // open: D, Q, clk, clr
  Register #(.width(32)) register_5 (.en(or_5_out[0]));  // open: D, Q, clk, clr
  Register #(.width(32)) register_6 (.en(or_6_out[0]));  // open: D, Q, clk, clr
  Register #(.width(32)) register_7 (.en(or_7_out[0]));  // open: D, Q, clk, clr
  Register #(.width(32)) register_8 (.en(or_8_out[0]));  // open: D, Q, clk, clr
  Register #(.width(32)) register_9 (.en(or_9_out[0]));  // open: D, Q, clk, clr
  Register #(.width(32)) register_10 (.en(or_10_out[0]));  // open: D, Q, clk, clr
  Register #(.width(32)) register_11 (.en(or_11_out[0]));  // open: D, Q, clk, clr
  Register #(.width(32)) register_12 (.en(or_12_out[0]));  // open: D, Q, clk, clr
  Register #(.width(32)) register_13 (.en(or_13_out[0]));  // open: D, Q, clk, clr
  Register #(.width(32)) register_14 (.en(or_14_out[0]));  // open: D, Q, clk, clr
  Register #(.width(32)) register_15 (.en(or_15_out[0]));  // open: D, Q, clk, clr
  Register #(.width(32)) register_16 (.en(or_16_out[0]));  // open: D, Q, clk, clr
  Register #(.width(32)) register_17 (.en(or_17_out[0]));  // open: D, Q, clk, clr
  Register #(.width(32)) register_18 (.en(or_18_out[0]));  // open: D, Q, clk, clr
  Register #(.width(32)) register_19 (.en(or_19_out[0]));  // open: D, Q, clk, clr
  Register #(.width(32)) register_20 (.en(or_20_out[0]));  // open: D, Q, clk, clr
  Register #(.width(32)) register_21 (.en(or_21_out[0]));  // open: D, Q, clk, clr
  Register #(.width(32)) register_22 (.en(or_22_out[0]));  // open: D, Q, clk, clr
  Register #(.width(32)) register_23 (.en(or_23_out[0]));  // open: D, Q, clk, clr
  Register #(.width(32)) register_24 (.en(or_24_out[0]));  // open: D, Q, clk, clr
  Register #(.width(32)) register_25 (.en(or_25_out[0]));  // open: D, Q, clk, clr
  Register #(.width(32)) register_26 (.en(or_26_out[0]));  // open: D, Q, clk, clr
  Register #(.width(32)) register_27 (.en(or_27_out[0]));  // open: D, Q, clk, clr
  Register #(.width(32)) register_28 (.en(or_28_out[0]));  // open: D, Q, clk, clr
  Register #(.width(32)) register_29 (.en(or_29_out[0]));  // open: D, Q, clk, clr
  Register #(.width(32)) register_30 (.en(or_30_out[0]));  // open: D, Q, clk, clr
  Register #(.width(32)) register_31 (.en(or_31_out[0]));  // open: D, Q, clk, clr
  Register #(.width(32)) register_32 (.en(or_32_out[0]));  // open: D, Q, clk, clr
endmodule
