// Logisim project decode unit.circ as structural Verilog: 1 circuit, main circuit main
module main (
  input  [6:0] Opcode,
  output [2:0] Format__type,
  output [3:0] Instruction_type
);

  wire comparator_1_eq, comparator_2_eq, comparator_3_eq, comparator_4_eq, comparator_5_eq, comparator_6_eq,
       comparator_7_eq, comparator_8_eq, comparator_9_eq, not_1_out, not_2_out, not_3_out, not_4_out,
       not_5_out, not_6_out, not_7_out, not_8_out, not_9_out, not_10_out, not_11_out, not_12_out, not_13_out,
       not_14_out, not_15_out, not_16_out, not_17_out, not_18_out, not_19_out, not_20_out, not_21_out,
       not_22_out, not_23_out, not_24_out, not_25_out, not_26_out, not_27_out, not_28_out, not_29_out,
       not_30_out, or_1_out, or_2_out;

  Comparator #(.width(7)) comparator_1 (.a(Opcode), .b(7'b0110011), .eq(comparator_1_eq));  // open: gt, lt
  Comparator #(.width(7)) comparator_2 (.a(Opcode), .b(7'b1100111), .eq(comparator_2_eq));  // open: gt, lt
  Comparator #(.width(7)) comparator_3 (.a(Opcode), .b(7'b0000011), .eq(comparator_3_eq));  // open: gt, lt
  Comparator #(.width(7)) comparator_4 (.a(Opcode), .b(7'b0010011), .eq(comparator_4_eq));  // open: gt, lt
  Comparator #(.width(7)) comparator_5 (.a(Opcode), .b(7'b0100011), .eq(comparator_5_eq));  // open: gt, lt
  Comparator #(.width(7)) comparator_6 (.a(Opcode), .b(7'b1100011), .eq(comparator_6_eq));  // open: gt, lt
  Comparator #(.width(7)) comparator_7 (.a(Opcode), .b(7'b0110111), .eq(comparator_7_eq));  // open: gt, lt
  Comparator #(.width(7)) comparator_8 (.a(Opcode), .b(7'b0010111), .eq(comparator_8_eq));  // open: gt, lt
  Comparator #(.width(7)) comparator_9 (.a(Opcode), .b(7'b1101111), .eq(comparator_9_eq));  // open: gt, lt
  or or_1 (or_1_out, comparator_2_eq, comparator_3_eq, comparator_4_eq);
  or or_2 (or_2_out, comparator_7_eq, comparator_8_eq);
  not not_1 (not_1_out, comparator_1_eq);
  not not_2 (not_2_out, or_1_out);
  not not_3 (not_3_out, comparator_5_eq);
  not not_4 (not_4_out, comparator_1_eq);
  not not_5 (not_5_out, comparator_6_eq);
  not not_6 (not_6_out, or_2_out);
  not not_7 (not_7_out, or_1_out);
  not not_8 (not_8_out, comparator_6_eq);
  not not_9 (not_9_out, comparator_9_eq);
  not not_10 (not_10_out, comparator_1_eq);
  not not_11 (not_11_out, comparator_2_eq);
  not not_12 (not_12_out, comparator_3_eq);
  not not_13 (not_13_out, comparator_4_eq);
  not not_14 (not_14_out, comparator_5_eq);
  not not_15 (not_15_out, comparator_6_eq);
  not not_16 (not_16_out, comparator_7_eq);
  not not_17 (not_17_out, comparator_1_eq);
  not not_18 (not_18_out, comparator_2_eq);
  not not_19 (not_19_out, comparator_3_eq);
  not not_20 (not_20_out, comparator_8_eq);
  not not_21 (not_21_out, comparator_9_eq);
  not not_22 (not_22_out, comparator_1_eq);
  not not_23 (not_23_out, comparator_4_eq);
  not not_24 (not_24_out, comparator_5_eq);
  not not_25 (not_25_out, comparator_8_eq);
  not not_26 (not_26_out, comparator_9_eq);
  not not_27 (not_27_out, comparator_2_eq);
  not not_28 (not_28_out, comparator_4_eq);
  not not_29 (not_29_out, comparator_6_eq);
  not not_30 (not_30_out, comparator_8_eq);
  and and_1 (Format__type[2], not_1_out, not_2_out, not_3_out);
  and and_2 (Format__type[1], not_4_out, not_5_out, not_6_out);
  and and_3 (Format__type[0], not_7_out, not_8_out, not_9_out);
  and and_4 (Instruction_type[3], not_10_out, not_11_out, not_12_out, not_13_out, not_14_out, not_15_out, not_16_out);
  and and_5 (Instruction_type[2], not_17_out, not_18_out, not_19_out, not_20_out, not_21_out);
  and and_6 (Instruction_type[1], not_22_out, not_23_out, not_24_out, not_25_out, not_26_out);
  and and_7 (Instruction_type[0], not_27_out, not_28_out, not_29_out, not_30_out);

  // Notes on the sheet:
  //   Format__type: pull=up
  //   R-type
  //   I type Jump
  //   I type Load
  //   I type ALU
  //   S-type
  //   B-type
  //   U -type LUI
  //   U-type AUPIC
  //   J-type
  //   I-type
  //   U-type
endmodule
