// Logisim project 32-bit ALU design.circ as structural Verilog: 1 circuit, main circuit 32 bit ALU
module _32_bit_ALU (
  input  [31:0] in_1,
  input  [31:0] in_2,
  input  [31:0] in_3,
  input  [3:0] in_4,
  output [31:0] out_5
);

  wire [6:0] comparator_1_eq;
  wire [7:0] comparator_1_gt, comparator_1_lt, comparator_2_lt, undriven, undriven_2, undriven_3, undriven_5,
       undriven_6, undriven_7, undriven_8, undriven_9, undriven_10, undriven_11, undriven_12;
  wire [8:0] undriven_4;
  wire [31:0] adder_1_out, and_1_out, divider_1_out, divider_1_rem, multiplier_1_out, or_1_out,
       shifter_1_out, shifter_2_out, shifter_3_out, subtractor_1_out, xor_1_out;

  assign or_1_out = in_2 | in_3;  // OR_Gate or_1, 32 bits wide
  assign and_1_out = in_2 & in_3;  // AND_Gate and_1, 32 bits wide
  assign xor_1_out = in_2 ^ in_3;  // XOR_Gate xor_1, 32 bits wide
  Adder #(.width(32)) adder_1 (.a(in_2), .b(in_3), .out(adder_1_out), .cin(in_1[0]));  // open: cout
  Subtractor #(.width(32)) subtractor_1 (.a(in_2), .b(in_3), .out(subtractor_1_out), .bin(in_1[0]));  // open: bout
  Multiplier #(.width(32)) multiplier_1 (.a(in_2), .b(in_3), .out(multiplier_1_out), .cin(in_1));  // open: cout
  Divider #(.width(32)) divider_1 (.a(in_2), .b(in_3), .out(divider_1_out), .upper(in_1), .rem(divider_1_rem));
  Comparator #(.width(32)) comparator_1 (
    .a(in_2), .b(in_3), .gt(comparator_1_gt[0]), .eq(comparator_1_eq[0]), .lt(comparator_1_lt[0]));
  Comparator #(.width(32), .mode("unsigned")) comparator_2 (
    .a(in_2), .b(in_3), .lt(comparator_2_lt[0]));  // open: gt, eq
  Shifter #(.width(32)) shifter_1 (.in(in_2), .\dist (in_3[4:0]), .out(shifter_1_out));
  Shifter #(.width(32), .shift("lr")) shifter_2 (.in(in_2), .\dist (in_3[4:0]), .out(shifter_2_out));
  Shifter #(.width(32), .shift("ar")) shifter_3 (.in(in_2), .\dist (in_3[4:0]), .out(shifter_3_out));
  Multiplexer #(.select(4), .width(32)) multiplexer_1 (
    .in0(or_1_out), .in1(and_1_out), .in2(xor_1_out), .in3(adder_1_out), .in4(subtractor_1_out),
    .in5(multiplier_1_out), .in6(divider_1_out), .in7(divider_1_rem),
    .in8({undriven_3, undriven_2, undriven, comparator_1_gt}),
    .in9({undriven_6, undriven_5, undriven_4, comparator_1_eq}),
    .in10({undriven_9, undriven_8, undriven_7, comparator_1_lt}),
    .in11({undriven_12, undriven_11, undriven_10, comparator_2_lt}), .in12(shifter_1_out),
    .in13(shifter_2_out), .in14(shifter_3_out), .out(out_5), .sel(in_4));  // open: in15, en

  // Notes on the sheet:
  //   OR
  //   And
  //   XOR
  //   ADD
  //   SUB
  //   MUL
  //   DIV
  //   REM
  //   BGT
  //   BEQ
  //   BLT/SLT
  //   SLTU
  //   SLL
  //   SRL
  //   SRA
endmodule
